# Fritzing sketch boatshare-sketch (saved by Fritzing 0.9.3b)
breadboards: 1

parts:
  Part1 = Photon
  Part2 = songle relay
  SIM7600e = Adafruit FONA 808 Breakout

nets:
  N1: Part1.RX, SIM7600e.TXD
  N2: Part1.TX, SIM7600e.RXD
  GND: Part1.GND, Part2.GND, SIM7600e.GND, SIM7600e.Speaker-
  VIN: Part1.VIN, Part2.VCC, SIM7600e.+5V
  N3: Part1.D6, Part2.COMMON

notes:
  Fant ikke riktig modul i fritzing. Benytter Adafruit FONA.
  Jeg benyttet meg av en egen usb-kabel til modulen for å gi nok strøm.
  GND
  SRD-05VDC-SL-C
  Songle relay

custom parts:
  Adafruit FONA 808 Breakout: Cellular + GPS tracking, all in one? Oh yes! Introducing Adafruit FONA 808 MiniGSM + GPS, an all-in-one cellular phone module with that lets you add location-tracking, voice, text, SMS and data to your project in an adorable little package.
